# Fritzing sketch Navigation System Schematic (saved by Fritzing 0.9.9b)

parts:
  Mod1 = Raspberry Pi 4B  # not connected
  J2 = Basic Servo
  ESC2 = ESC 30A
  ESC4 = ESC 30A
  J3 = Basic Servo
  Part4 = Arduino XBee Shield
  U3 = XBEE-1 [package=xbee-silk]  # not connected
  ANT1 = Antenna  # not connected
  Part5 = Arduino XBee Shield  # not connected
  U4 = XBEE-1 [package=xbee-silk]  # not connected
  ANT2 = Antenna  # not connected
  U2 = 74HC4052 [package=dil16]
  U5 = AVR 10-pin ICSP Header [package="avr icsp"]
  Part6 = Arduino Uno (Rev3)

nets:
  N1: J2.gnd, ESC2.A
  N2: J2.vcc, ESC2.B
  N3: J2.pulse, ESC2.C
  N4: ESC2.In, U2.Y0
  GND: ESC4.v+, ESC4.GND, U2.GND
  N5: ESC4.A, J3.gnd
  N6: ESC4.B, J3.vcc
  N7: ESC4.C, J3.pulse
  N8: ESC4.In, U2.X0
  N9: Part4.D_TX, U2.X
  N10: Part4.D4, U2.Y
  N11: Part4.UART_RX, Part6.D1/TX
  N12: Part4.UART_TX, Part6.D0/RX
  N13: U2.Y2, U5.3
  N14: U2.A, U5.5
  N15: U2.X1, U5.1

notes:
  Raspberry Pi 4
  Blue Robotics Basic ESC
  simpleRTK2b Base
  with XBee Radio and antenna
  simpleRTK2b Rover with Xbee radio and antenna
  Dual 4 channel mux
  RC Receiver
  Blue Robotics T200 Thruster
  Transmitting Arduino Uno

custom parts:
  ESC 30A: Electronic Speed Controller - 30A
